// Logisim project EX.circ as structural Verilog: 4 circuits, main circuit main
module main (
  input  in_1,
  input  in_2,
  input  in_3,
  input  in_4,
  input  in_5,
  input  [12:0] in_6,
  input  [1:0] in_7,
  input  [31:0] Data,
  input  [1:0] in_9,
  input  [31:0] in_10,
  input  [31:0] in_11,
  input  [31:0] in_12,
  input  [31:0] in_13,
  input  [31:0] in_14,
  output out_15,
  output [31:0] out_16,
  output [31:0] out_17,
  output [31:0] out_18
);

  wire alu_1_iseq, alu_1_isgt, flags_1_flags_e, flags_1_flags_gt;
  wire [31:0] multiplexer_1_out, multiplexer_2_out;

  Multiplexer #(.select(2), .width(32), .enable("false")) multiplexer_1 (
    .in0(in_13), .in1(Data), .in2(in_14), .in3(in_14), .out(multiplexer_1_out), .sel(in_7));
  Multiplexer #(.select(2), .width(32), .enable("false")) multiplexer_2 (
    .in0(in_12), .in1(Data), .in2(in_14), .in3(in_14), .out(multiplexer_2_out), .sel(in_9));
  Multiplexer #(.width(32), .enable("false")) multiplexer_3 (.in0(in_11), .in1(Data), .out(out_17), .sel(in_5));
  ALU alu_1 (
    .A(multiplexer_2_out), .B(multiplexer_1_out), .ALU_Signals(in_6), .ALU_Result(out_16), .isGT(alu_1_isgt),
    .isEQ(alu_1_iseq));
  Multiplexer #(.width(32), .enable("false")) multiplexer_4 (
    .in0(in_10), .in1(multiplexer_2_out), .out(out_18), .sel(in_1));
  Flags flags_1 (
    .isCmp(in_6[0]), .is(alu_1_isgt), .is_2(alu_1_iseq), .flags_GT(flags_1_flags_gt),
    .flags_E(flags_1_flags_e));
  Branch_Unit branch_unit_1 (
    .isUBranch(in_4), .isBeq(in_2), .flags_E(flags_1_flags_gt), .isBgt(in_3), .flags_GT(flags_1_flags_e),
    .isBranchTaken(out_15));

  // Other names for the same wires on the sheet: A[31:0] = in_12; aluResult[31:0] = out_16; aluResultIn[31:0] = in_14;
  //   ALUsignals[12:0] = in_6; B[31:0] = in_13; branch_Target[31:0] = in_10; branch_TargetOut[31:0] = out_18;
  //   isBeq = in_2; isBgt = in_3; isBranchTaken = out_15; isRet = in_1; isUBranch = in_4; op2[31:0] = in_11;
  //   op2Out[31:0] = out_17; RW__EX_op2 = in_5; RW_MA__EX_op1[1:0] = in_9; RW_MA__EX_op2[1:0] = in_7

  // Notes on the sheet:
  //   aluResult
  //   ALUsignals
  //   B
  //   A
  //   isRet
  //   isGT
  //   isEQ
  //   flags(GT)
  //   flags(E)
  //   isBeq
  //   isBgt
  //   isUBranch
endmodule

module Branch_Unit (
  input  isUBranch,
  input  isBeq,
  input  flags_E,
  input  isBgt,
  input  flags_GT,
  output isBranchTaken
);

  wire and_1_out, and_2_out;

  and and_1 (and_1_out, isBeq, flags_E);
  and and_2 (and_2_out, isBgt, flags_GT);
  or or_1 (isBranchTaken, isUBranch, and_1_out, and_2_out);
endmodule

module ALU (
  input  [31:0] A,
  input  [31:0] B,
  input  [12:0] ALU_Signals,
  output [31:0] ALU_Result,
  output isGT,
  output isEQ
);

  wire [31:0] adder_1_out, and_1_out, divider_1_out, divider_1_rem, multiplier_1_out, not_1_out, or_1_out,
       shifter_1_out, shifter_2_out, shifter_3_out, subtractor_1_out;

  Adder #(.width(32)) adder_1 (.a(A), .b(B), .out(adder_1_out));  // open: cin, cout
  Subtractor #(.width(32)) subtractor_1 (.a(A), .b(B), .out(subtractor_1_out));  // open: bin, bout
  Multiplier #(.width(32)) multiplier_1 (.a(A), .b(B), .out(multiplier_1_out));  // open: cin, cout
  Divider #(.width(32)) divider_1 (.a(A), .b(B), .out(divider_1_out), .rem(divider_1_rem));  // open: upper
  Comparator #(.width(32)) comparator_1 (.a(A), .b(B), .gt(isGT), .eq(isEQ));  // open: lt
  Shifter #(.width(32)) shifter_1 (.in(A), .\dist (B[4:0]), .out(shifter_1_out));
  Shifter #(.width(32), .shift("lr")) shifter_2 (.in(A), .\dist (B[4:0]), .out(shifter_2_out));
  Shifter #(.width(32), .shift("ar")) shifter_3 (.in(A), .\dist (B[4:0]), .out(shifter_3_out));
  assign not_1_out = ~B;  // NOT_Gate not_1, 32 bits wide
  assign and_1_out = A & B;  // AND_Gate and_1, 32 bits wide
  assign or_1_out = A | B;  // OR_Gate or_1, 32 bits wide
  assign ALU_Result = ALU_Signals[1] ? adder_1_out : 32'bz;  // Controlled_Buffer controlled_buffer_1
  assign ALU_Result = ALU_Signals[2] ? subtractor_1_out : 32'bz;  // Controlled_Buffer controlled_buffer_2
  assign ALU_Result = ALU_Signals[3] ? multiplier_1_out : 32'bz;  // Controlled_Buffer controlled_buffer_3
  assign ALU_Result = ALU_Signals[4] ? divider_1_out : 32'bz;  // Controlled_Buffer controlled_buffer_4
  assign ALU_Result = ALU_Signals[5] ? divider_1_rem : 32'bz;  // Controlled_Buffer controlled_buffer_5
  assign ALU_Result = ALU_Signals[6] ? B : 32'bz;  // Controlled_Buffer controlled_buffer_6
  assign ALU_Result = ALU_Signals[7] ? shifter_1_out : 32'bz;  // Controlled_Buffer controlled_buffer_7
  assign ALU_Result = ALU_Signals[8] ? shifter_2_out : 32'bz;  // Controlled_Buffer controlled_buffer_8
  assign ALU_Result = ALU_Signals[9] ? shifter_3_out : 32'bz;  // Controlled_Buffer controlled_buffer_9
  assign ALU_Result = ALU_Signals[10] ? not_1_out : 32'bz;  // Controlled_Buffer controlled_buffer_10
  assign ALU_Result = ALU_Signals[11] ? and_1_out : 32'bz;  // Controlled_Buffer controlled_buffer_11
  assign ALU_Result = ALU_Signals[12] ? or_1_out : 32'bz;  // Controlled_Buffer controlled_buffer_12

  // Notes on the sheet:
  //   add
  //   sub
  //   mul
  //   div
  //   cmp
  //   lsr
  //   mod
  //   lsl
  //   asr
endmodule

module Flags (
  input  isCmp,
  input  is,
  input  is_2,
  output flags_GT,
  output flags_E
);

  D_Flip_Flop #(.trigger("high")) d_ff_1 (.clk(isCmp), .D(is), .Q(flags_GT));  // open: Qn, preset, en, reset
  D_Flip_Flop #(.trigger("high")) d_ff_2 (.clk(isCmp), .D(is_2), .Q(flags_E));  // open: Qn, preset, en, reset
endmodule
